# Fritzing sketch coroutine_led_lamp_fx (saved by Fritzing 0.9.4)
breadboards: 1

parts:
  Part1 = Arduino Nano (Rev3.0)
  LED1 = LED - 3mm [color="Green (555nm)" package="3 mm [THT]"]
  R1 = Resistor [tolerance=±5% resistance=1k package="0402 [SMD]"]
  R2 = Resistor [tolerance=±5% resistance=1k package="0402 [SMD]"]
  LED2 = LED - 3mm [color="Red (633nm)" package="3 mm [THT]"]

nets:
  N1: Part1.D4, LED1.anode
  N2: Part1.D5, LED2.anode
  VIN: Part1.VIN, Part1.GND
  N3: LED1.cathode, R1.Pin_1
  N4: R1.Pin_0, R2.Pin_0
  N5: R2.Pin_1, LED2.cathode
